# Fritzing sketch Layout (saved by Fritzing 0.9.4)
breadboards: 1

parts:
  Bauteil1 = Arduino Uno (Rev3)
  LED1 = LED - 5mm [color="Red (633nm)" package="5 mm [THT]"]
  LED2 = LED - 5mm [color="Yellow (595nm)" package="5 mm [THT]"]
  LED3 = LED - 5mm [color="Green (570nm)" package="5 mm [THT]"]
  LCD1 = LCD screen
  S2 = Pushbutton [package="[THT]"]
  S3 = Pushbutton [package="[THT]"]
  R1 = Resistor [tolerance=±5% resistance=330 package=THT]
  R2 = Resistor [tolerance=±5% resistance=330 package=THT]
  R3 = Resistor [tolerance=±5% resistance=330 package=THT]
  R4 = Resistor [tolerance=±5% resistance=2.0k package=THT]
  R5 = Resistor [tolerance=±5% resistance=2.0k package=THT]
  Bauteil2 = Adafruit CCS811
  LED4 = LED - 5mm [color="Blue (525nm)" package="5 mm [THT]"]
  R7 = Resistor [tolerance=±5% resistance=330 package=THT]
  microSD1 = MicroSD Card Module
  R9 = Resistor [tolerance=±5% resistance=2.0k package=THT]
  S4 = Pushbutton [package="[THT]"]
  LCM1602_IIC1 = LCM1602 IIC [part_number="LCM1602 IIC" chip_label="LCM1602 IIC" package="DIP (Dual Inline) [THT]"]

nets:
  N1: Bauteil1.A0, LCM1602_IIC1.SCL
  N2: Bauteil1.A1, LCM1602_IIC1.SDA
  N3: Bauteil1.A2, R1.Pin_0
  N4: Bauteil1.A3, R2.Pin_0
  N5: Bauteil1.A4/SDA, R3.Pin_0, Bauteil2.SDA
  N6: Bauteil1.A5/SCL, Bauteil2.SCL, R7.Pin_0
  N7: Bauteil1.D8, S2.Pin_1, S2.Pin_2, R5.Pin_0
  N8: Bauteil1.D9_PWM, R9.Pin_0, S4.Pin_1, S4.Pin_2
  N9: Bauteil1.D11_PWM/MOSI, microSD1.SCK
  N10: Bauteil1.D12/MISO, microSD1.MOSI
  N11: Bauteil1.D13/SCK, microSD1.MISO
  GND: Bauteil1.GND, LED1.anode, LED2.anode, LED3.anode, R4.Pin_1, R5.Pin_1, Bauteil2.GND, Bauteil2.!WAKE, LED4.anode, microSD1.GND, R9.Pin_1, LCM1602_IIC1.GND
  N12: Bauteil1.D2, S3.Pin_1, S3.Pin_2, R4.Pin_0
  N13: Bauteil1.D5_PWM, microSD1.CS
  3V3: Bauteil1.3V3, Bauteil2.3.3V
  VCC: Bauteil1.5V, S2.Pin_3, S2.Pin_4, S3.Pin_3, S3.Pin_4, microSD1.VCC, S4.Pin_3, S4.Pin_4, LCM1602_IIC1.VCC
  N14: LED1.cathode, R1.Pin_1
  N15: LED2.cathode, R2.Pin_1
  N16: LED3.cathode, R3.Pin_1
  VSS: LCD1.VSS, LCM1602_IIC1.VSS
  VDD: LCD1.VDD, LCM1602_IIC1.VDD
  N17: LCD1.V0, LCM1602_IIC1.V0
  N18: LCD1.RS, LCM1602_IIC1.RS
  N19: LCD1.R/W, LCM1602_IIC1.RW
  N20: LCD1.E, LCM1602_IIC1.E
  N21: LCD1.DB0, LCM1602_IIC1.D0
  N22: LCD1.DB1, LCM1602_IIC1.D1
  N23: LCD1.DB2, LCM1602_IIC1.D2
  N24: LCD1.DB3, LCM1602_IIC1.D3
  N25: LCD1.DB4, LCM1602_IIC1.D4
  N26: LCD1.DB5, LCM1602_IIC1.D5
  N27: LCD1.DB6, LCD1.DB7, LCM1602_IIC1.D6, LCM1602_IIC1.D7
  N28: LCD1.LED+, LCM1602_IIC1.A
  N29: LCD1.LED-, LCM1602_IIC1.K
  N30: LED4.cathode, R7.Pin_1

custom parts:
  LCM1602 IIC: I2C-Module to use a 1602 or 2004 LCD on with the wire.h libory Serial LCD Modul
